// Logisim project Universal_Shift_Register_DFF.circ as structural Verilog: 1 circuit, main circuit main
module main (
  input  ShiftRight,
  input  I3,
  input  I2,
  input  I1,
  input  ShiftLeft,
  input  I0,
  input  [1:0] Selectors,
  output O3,
  output O2,
  output O1,
  output O0
);

  wire Clk_out, multiplexer_1_out, multiplexer_2_out, multiplexer_3_out, multiplexer_4_out;

  Multiplexer #(.select(2)) multiplexer_1 (
    .in0(O3), .in1(ShiftRight), .in2(O2), .in3(I3), .out(multiplexer_1_out), .sel(Selectors));
  Multiplexer #(.select(2)) multiplexer_2 (
    .in0(O2), .in1(O3), .in2(O1), .in3(I2), .out(multiplexer_2_out), .sel(Selectors));
  Multiplexer #(.select(2)) multiplexer_3 (
    .in0(O1), .in1(O2), .in2(O0), .in3(I1), .out(multiplexer_3_out), .sel(Selectors));
  Multiplexer #(.select(2)) multiplexer_4 (
    .in0(O0), .in1(O1), .in2(ShiftLeft), .in3(I0), .out(multiplexer_4_out), .sel(Selectors));
  D_Flip_Flop D3 (.D(multiplexer_1_out), .clk(Clk_out), .Q(O3));  // open: Qn, preset, reset
  D_Flip_Flop D2 (.D(multiplexer_2_out), .clk(Clk_out), .Q(O2));  // open: Qn, preset, reset
  D_Flip_Flop D1 (.D(multiplexer_3_out), .clk(Clk_out), .Q(O1));  // open: Qn, preset, reset
  D_Flip_Flop D0 (.D(multiplexer_4_out), .clk(Clk_out), .Q(O0));  // open: Qn, preset, reset
  Clock Clk (.out(Clk_out));

  // Notes on the sheet:
  //   Selector: \n Tirth
endmodule
